// Logisim project BCD.circ as structural Verilog: 1 circuit, main circuit main
module main (
  input  A,
  input  B,
  input  C,
  input  D
);

  wire and_1_out, and_2_out, and_3_out, and_4_out, and_5_out, and_6_out, and_7_out, not_1_out, not_2_out,
       not_3_out, not_4_out, not_5_out, or_1_out, or_2_out, or_3_out, or_4_out, or_5_out, or_6_out, or_7_out,
       xnor_1_out, xnor_2_out, xor_1_out;

  not not_1 (not_1_out, B);
  and and_1 (and_1_out, not_1_out, C);
  or or_1 (or_1_out, A, C, xnor_1_out);
  or or_2 (or_2_out, not_1_out, xnor_2_out);
  xnor xnor_1 (xnor_1_out, B, D);
  xnor xnor_2 (xnor_2_out, C, D);
  not not_2 (not_2_out, D);
  not not_3 (not_3_out, C);
  not not_4 (not_4_out, C);
  not not_5 (not_5_out, D);
  and and_2 (and_2_out, C, not_2_out);
  and and_3 (and_3_out, D, B, not_3_out);
  or or_3 (or_3_out, B, not_3_out, D);
  xor xor_1 (xor_1_out, C, B);
  and and_4 (and_4_out, not_4_out, not_5_out);
  and and_5 (and_5_out, not_2_out, not_1_out);
  or or_4 (or_4_out, and_1_out, A, and_3_out, and_2_out, and_5_out);
  or or_5 (or_5_out, and_5_out, and_2_out);
  or or_6 (or_6_out, and_2_out, A, xor_1_out);
  and and_6 (and_6_out, not_5_out, B);
  and and_7 (and_7_out, not_4_out, B);
  or or_7 (or_7_out, A, and_4_out, and_6_out, and_7_out);
  _7_Segment_Display u_7_segment_display_1 (
    .g(or_6_out), .f(or_7_out), .a(or_1_out), .b(or_2_out), .e(or_5_out), .d(or_4_out), .c(or_3_out));  // open: dp
endmodule
