// Logisim project BCDic.circ as structural Verilog: 1 circuit, main circuit main
module main (
  input  A,
  input  B,
  input  C,
  input  D,
  output out_5,
  output out_6,
  output out_7,
  output out_8,
  output out_9,
  output out_10,
  output out_11
);

  wire and_1_out, and_2_out, and_3_out, and_4_out, and_5_out, and_6_out, and_7_out, not_1_out, not_2_out,
       not_3_out, not_4_out, not_5_out, xnor_1_out, xnor_2_out, xor_1_out;

  not not_1 (not_1_out, B);
  and and_1 (and_1_out, not_1_out, C);
  or or_1 (out_5, A, C, xnor_1_out);
  or or_2 (out_6, not_1_out, xnor_2_out);
  xnor xnor_1 (xnor_1_out, B, D);
  xnor xnor_2 (xnor_2_out, C, D);
  not not_2 (not_2_out, D);
  not not_3 (not_3_out, C);
  not not_4 (not_4_out, C);
  not not_5 (not_5_out, D);
  and and_2 (and_2_out, C, not_2_out);
  and and_3 (and_3_out, D, B, not_3_out);
  or or_3 (out_7, B, not_3_out, D);
  xor xor_1 (xor_1_out, C, B);
  and and_4 (and_4_out, not_4_out, not_5_out);
  and and_5 (and_5_out, not_2_out, not_1_out);
  or or_4 (out_8, and_1_out, A, and_3_out, and_2_out, and_5_out);
  or or_5 (out_9, and_5_out, and_2_out);
  or or_6 (out_11, and_2_out, A, xor_1_out);
  and and_6 (and_6_out, not_5_out, B);
  and and_7 (and_7_out, not_4_out, B);
  or or_7 (out_10, A, and_4_out, and_6_out, and_7_out);
endmodule
