// Logisim project Digital Clock.circ as structural Verilog: 1 circuit, main circuit main
module main (
  input  in_1,
  input  in_2,
  input  in_3,
  input  in_4,
  input  in_5,
  input  in_6,
  input  in_7,
  input  in_8,
  input  in_9
);

  wire and_1_out, clock_1_out, dip_7411_1_p4, dip_7411_2_p4, dip_7421_1_p5, dip_7421_2_p5, dip_7421_3_p5,
       dip_7421_3_p10, main_1_out_5, main_1_out_6, main_1_out_7, main_1_out_8, main_1_out_9, main_1_out_10,
       main_1_out_11, main_2_out_5, main_2_out_6, main_2_out_7, main_2_out_8, main_2_out_9, main_2_out_10,
       main_2_out_11, main_3_out_5, main_3_out_6, main_3_out_7, main_3_out_8, main_3_out_9, main_3_out_10,
       main_3_out_11, main_4_out_5, main_4_out_6, main_4_out_7, main_4_out_8, main_4_out_9, main_4_out_10,
       main_4_out_11, main_5_out_5, main_5_out_6, main_5_out_7, main_5_out_8, main_5_out_9, main_5_out_10,
       main_5_out_11, main_6_out_5, main_6_out_6, main_6_out_7, main_6_out_8, main_6_out_9, main_6_out_10,
       main_6_out_11, or_1_out, t_ff_1_q, t_ff_1_qn, t_ff_2_q, t_ff_2_qn, t_ff_3_q, t_ff_3_qn, t_ff_4_q,
       t_ff_5_q, t_ff_5_qn, t_ff_6_q, t_ff_6_qn, t_ff_7_q, t_ff_7_qn, t_ff_8_q, t_ff_8_qn, t_ff_9_q,
       t_ff_9_qn, t_ff_10_q, t_ff_10_qn, t_ff_11_q, t_ff_11_qn, t_ff_12_q, t_ff_12_qn, t_ff_13_q, t_ff_14_q,
       t_ff_15_q, t_ff_15_qn, t_ff_16_q, t_ff_17_q, t_ff_17_qn, t_ff_18_q, t_ff_19_q, t_ff_19_qn;

  Clock clock_1 (.out(clock_1_out));
  T_Flip_Flop t_ff_1 (
    .clk(clock_1_out), .T(in_1), .Q(t_ff_1_q), .Qn(t_ff_1_qn), .reset(dip_7421_1_p5), .en(in_1));  // open: preset
  T_Flip_Flop t_ff_2 (
    .clk(dip_7421_1_p5), .T(in_3), .Q(t_ff_2_q), .Qn(t_ff_2_qn), .reset(dip_7411_1_p4), .en(in_3));  // open: preset
  T_Flip_Flop t_ff_3 (
    .clk(dip_7411_1_p4), .T(in_4), .Q(t_ff_3_q), .Qn(t_ff_3_qn), .reset(dip_7421_2_p5), .en(in_4));  // open: preset
  T_Flip_Flop t_ff_4 (.clk(dip_7421_3_p5), .T(in_9), .Q(t_ff_4_q), .reset(and_1_out), .en(in_9));  // open: Qn, preset
  T_Flip_Flop t_ff_5 (
    .clk(t_ff_1_qn), .T(in_1), .Q(t_ff_5_q), .Qn(t_ff_5_qn), .reset(dip_7421_1_p5), .en(in_1));  // open: preset
  T_Flip_Flop t_ff_6 (
    .clk(t_ff_2_qn), .T(in_3), .Q(t_ff_6_q), .Qn(t_ff_6_qn), .reset(dip_7411_1_p4), .en(in_3));  // open: preset
  T_Flip_Flop t_ff_7 (
    .clk(dip_7421_2_p5), .T(in_6), .Q(t_ff_7_q), .Qn(t_ff_7_qn), .reset(dip_7411_2_p4), .en(in_6));  // open: preset
  T_Flip_Flop t_ff_8 (
    .clk(dip_7411_2_p4), .T(in_7), .Q(t_ff_8_q), .Qn(t_ff_8_qn), .reset(or_1_out), .en(in_7));  // open: preset
  or or_1 (or_1_out, dip_7421_3_p5, and_1_out);
  T_Flip_Flop t_ff_9 (
    .clk(t_ff_5_qn), .T(in_1), .Q(t_ff_9_q), .Qn(t_ff_9_qn), .reset(dip_7421_1_p5), .en(in_1));  // open: preset
  T_Flip_Flop t_ff_10 (
    .clk(t_ff_3_qn), .T(in_4), .Q(t_ff_10_q), .Qn(t_ff_10_qn), .reset(dip_7421_2_p5), .en(in_4));  // open: preset
  T_Flip_Flop t_ff_11 (
    .clk(t_ff_7_qn), .T(in_6), .Q(t_ff_11_q), .Qn(t_ff_11_qn), .reset(dip_7411_2_p4), .en(in_6));  // open: preset
  T_Flip_Flop t_ff_12 (
    .clk(t_ff_8_qn), .T(in_7), .Q(t_ff_12_q), .Qn(t_ff_12_qn), .reset(or_1_out), .en(in_7));  // open: preset
  T_Flip_Flop t_ff_13 (.clk(t_ff_9_qn), .T(in_1), .Q(t_ff_13_q), .reset(dip_7421_1_p5), .en(in_1));  // open: Qn, preset
  T_Flip_Flop t_ff_14 (.clk(t_ff_6_qn), .T(in_3), .Q(t_ff_14_q), .reset(dip_7411_1_p4), .en(in_3));  // open: Qn, preset
  T_Flip_Flop t_ff_15 (
    .clk(t_ff_10_qn), .T(in_4), .Q(t_ff_15_q), .Qn(t_ff_15_qn), .reset(dip_7421_2_p5), .en(in_4));  // open: preset
  T_Flip_Flop t_ff_16 (
    .clk(t_ff_11_qn), .T(in_6), .Q(t_ff_16_q), .reset(dip_7411_2_p4), .en(in_6));  // open: Qn, preset
  T_Flip_Flop t_ff_17 (
    .clk(t_ff_12_qn), .T(in_7), .Q(t_ff_17_q), .Qn(t_ff_17_qn), .reset(or_1_out), .en(in_7));  // open: preset
  BCDic_main main_1 (
    .A(t_ff_13_q), .B(t_ff_9_q), .C(t_ff_5_q), .D(t_ff_1_q), .out_5(main_1_out_5), .out_6(main_1_out_6),
    .out_7(main_1_out_7), .out_8(main_1_out_8), .out_9(main_1_out_9), .out_10(main_1_out_10),
    .out_11(main_1_out_11));
  T_Flip_Flop t_ff_18 (
    .clk(t_ff_15_qn), .T(in_4), .Q(t_ff_18_q), .reset(dip_7421_2_p5), .en(in_4));  // open: Qn, preset
  _7_Segment_Display u_7_segment_display_1 (
    .g(main_1_out_11), .f(main_1_out_10), .a(main_1_out_5), .b(main_1_out_6), .e(main_1_out_9),
    .d(main_1_out_8), .c(main_1_out_7));  // open: dp
  BCDic_main main_2 (
    .A(in_2), .B(t_ff_14_q), .C(t_ff_6_q), .D(t_ff_2_q), .out_5(main_2_out_5), .out_6(main_2_out_6),
    .out_7(main_2_out_7), .out_8(main_2_out_8), .out_9(main_2_out_9), .out_10(main_2_out_10),
    .out_11(main_2_out_11));
  T_Flip_Flop t_ff_19 (
    .clk(t_ff_17_qn), .T(in_7), .Q(t_ff_19_q), .Qn(t_ff_19_qn), .reset(or_1_out), .en(in_7));  // open: preset
  // DIP_7421 dip_7421_1: pin names not known; wires that end beside it: t_ff_13_q, t_ff_9_qn, t_ff_5_q, t_ff_1_qn, dip_7421_1_p5
  _7_Segment_Display u_7_segment_display_2 (
    .g(main_2_out_11), .f(main_2_out_10), .a(main_2_out_5), .b(main_2_out_6), .e(main_2_out_9),
    .d(main_2_out_8), .c(main_2_out_7));  // open: dp
  // DIP_7411 dip_7411_1: pin names not known; wires that end beside it: t_ff_14_q, t_ff_6_q, t_ff_2_qn, dip_7411_1_p4
  BCDic_main main_3 (
    .A(t_ff_18_q), .B(t_ff_15_q), .C(t_ff_10_q), .D(t_ff_3_q), .out_5(main_3_out_5), .out_6(main_3_out_6),
    .out_7(main_3_out_7), .out_8(main_3_out_8), .out_9(main_3_out_9), .out_10(main_3_out_10),
    .out_11(main_3_out_11));
  // DIP_7421 dip_7421_2: pin names not known; wires that end beside it: t_ff_18_q, t_ff_15_qn, t_ff_10_q, t_ff_3_qn, dip_7421_2_p5, t_ff_7_q
  BCDic_main main_4 (
    .A(in_5), .B(t_ff_16_q), .C(t_ff_11_q), .D(t_ff_7_q), .out_5(main_4_out_5), .out_6(main_4_out_6),
    .out_7(main_4_out_7), .out_8(main_4_out_8), .out_9(main_4_out_9), .out_10(main_4_out_10),
    .out_11(main_4_out_11));
  // DIP_7411 dip_7411_2: pin names not known; wires that end beside it: t_ff_16_q, t_ff_11_q, t_ff_7_qn, dip_7411_2_p4
  // DIP_7421 dip_7421_3: pin names not known; wires that end beside it: t_ff_19_q, t_ff_17_qn, t_ff_12_q, t_ff_8_qn, dip_7421_3_p5, t_ff_19_qn, t_ff_17_qn, t_ff_12_q, t_ff_8_qn, dip_7421_3_p10
  _7_Segment_Display u_7_segment_display_3 (
    .g(main_3_out_11), .f(main_3_out_10), .a(main_3_out_5), .b(main_3_out_6), .e(main_3_out_9),
    .d(main_3_out_8), .c(main_3_out_7));  // open: dp
  _7_Segment_Display u_7_segment_display_4 (
    .g(main_4_out_11), .f(main_4_out_10), .a(main_4_out_5), .b(main_4_out_6), .e(main_4_out_9),
    .d(main_4_out_8), .c(main_4_out_7));  // open: dp
  and and_1 (and_1_out, dip_7421_3_p10, t_ff_4_q);
  BCDic_main main_5 (
    .A(in_8), .B(in_8), .C(in_8), .D(t_ff_4_q), .out_5(main_5_out_5), .out_6(main_5_out_6),
    .out_7(main_5_out_7), .out_8(main_5_out_8), .out_9(main_5_out_9), .out_10(main_5_out_10),
    .out_11(main_5_out_11));
  BCDic_main main_6 (
    .A(t_ff_19_q), .B(t_ff_17_q), .C(t_ff_12_q), .D(t_ff_8_q), .out_5(main_6_out_5), .out_6(main_6_out_6),
    .out_7(main_6_out_7), .out_8(main_6_out_8), .out_9(main_6_out_9), .out_10(main_6_out_10),
    .out_11(main_6_out_11));
  _7_Segment_Display u_7_segment_display_5 (
    .g(main_5_out_11), .f(main_5_out_10), .a(main_5_out_5), .b(main_5_out_6), .e(main_5_out_9),
    .d(main_5_out_8), .c(main_5_out_7));  // open: dp
  _7_Segment_Display u_7_segment_display_6 (
    .g(main_6_out_11), .f(main_6_out_10), .a(main_6_out_5), .b(main_6_out_6), .e(main_6_out_9),
    .d(main_6_out_8), .c(main_6_out_7));  // open: dp
endmodule
